// Logisim project StickyStacky16.circ as structural Verilog: 2 circuits, main circuit main
// fez
module main (
  input  [15:0] Input,
  input  [1:0] SPsel,
  input  Clock,
  input  [1:0] Wsel,
  output [15:0] stack_sp,
  output [15:0] stack_sp_2
);

  wire nand_1_out, r0ac, r1ac, r2ac, r3ac, r4ac, r5ac, r6ac, r7ac, r8ac, r9ac, r10ac, r11ac, r12ac, r13ac,
       r14ac, r15ac;
  wire [3:0] multiplexer_1_out, sp, sp_1, sp_1_t;
  wire [15:0] r0, r1, r2, r3, r4, r5, r6, r7, r8, r9, r10, r11, r12, r13, r14, r15;

  Multiplexer #(.select(2), .width(4), .enable("false")) multiplexer_1 (
    .in0(sp), .in1(sp_1_t), .in2(sp_1), .out(multiplexer_1_out), .sel(Wsel));  // open: in3
  Decoder #(.select(4), .disabled(0)) decoder_1 (
    .out0(r0ac), .out1(r1ac), .out2(r2ac), .out3(r3ac), .out4(r4ac), .out5(r5ac), .out6(r6ac), .out7(r7ac),
    .out8(r8ac), .out9(r9ac), .out10(r10ac), .out11(r11ac), .out12(r12ac), .out13(r13ac), .out14(r14ac),
    .out15(r15ac), .sel(multiplexer_1_out), .en(nand_1_out));
  nand nand_1 (nand_1_out, Wsel[0], Wsel[1]);
  Register #(.width(16)) register_1 (.D(Input), .en(r0ac), .Q(r0), .clk(Clock));  // open: clr
  Register #(.width(16)) register_2 (.D(Input), .en(r1ac), .Q(r1), .clk(Clock));  // open: clr
  Register #(.width(16)) register_3 (.D(Input), .en(r2ac), .Q(r2), .clk(Clock));  // open: clr
  Register #(.width(16)) register_4 (.D(Input), .en(r3ac), .Q(r3), .clk(Clock));  // open: clr
  Multiplexer #(.select(4), .width(16), .enable("false")) multiplexer_2 (
    .in0(r0), .in1(r1), .in2(r2), .in3(r3), .in4(r4), .in5(r5), .in6(r6), .in7(r7), .in8(r8), .in9(r9),
    .in10(r10), .in11(r11), .in12(r12), .in13(r13), .in14(r14), .in15(r15), .out(stack_sp), .sel(sp));
  Register #(.width(16)) register_5 (.D(Input), .en(r4ac), .Q(r4), .clk(Clock));  // open: clr
  SP_register sp_register_1 (.spsel(SPsel), .clock(Clock), .sp___1(sp_1), .sp(sp), .sp___1_2(sp_1_t));
  Register #(.width(16)) register_6 (.D(Input), .en(r5ac), .Q(r5), .clk(Clock));  // open: clr
  Register #(.width(16)) register_7 (.D(Input), .en(r7ac), .Q(r7), .clk(Clock));  // open: clr
  Register #(.width(16)) register_8 (.D(Input), .en(r6ac), .Q(r6), .clk(Clock));  // open: clr
  // Probe on sp_1
  // Probe on sp
  // Probe on sp_1_t
  Multiplexer #(.select(4), .width(16), .enable("false")) multiplexer_3 (
    .in0(r0), .in1(r1), .in2(r2), .in3(r3), .in4(r4), .in5(r5), .in6(r6), .in7(r7), .in8(r8), .in9(r9),
    .in10(r10), .in11(r11), .in12(r12), .in13(r13), .in14(r14), .in15(r15), .out(stack_sp_2), .sel(sp_1));
  Register #(.width(16)) register_9 (.D(Input), .en(r8ac), .Q(r8), .clk(Clock));  // open: clr
  Register #(.width(16)) register_10 (.D(Input), .en(r9ac), .Q(r9), .clk(Clock));  // open: clr
  Register #(.width(16)) register_11 (.D(Input), .en(r11ac), .Q(r11), .clk(Clock));  // open: clr
  Register #(.width(16)) register_12 (.D(Input), .en(r10ac), .Q(r10), .clk(Clock));  // open: clr
  Register #(.width(16)) register_13 (.D(Input), .en(r12ac), .Q(r12), .clk(Clock));  // open: clr
  Register #(.width(16)) register_14 (.D(Input), .en(r13ac), .Q(r13), .clk(Clock));  // open: clr
  Register #(.width(16)) register_15 (.D(Input), .en(r15ac), .Q(r15), .clk(Clock));  // open: clr
  Register #(.width(16)) register_16 (.D(Input), .en(r14ac), .Q(r14), .clk(Clock));  // open: clr

  // Notes on the sheet:
  //   r[n]ac = 1 si le registre [n] est actif, 0 sinon
endmodule

module SP_register (
  input  [1:0] spsel,
  input  clock,
  output [3:0] sp___1,
  output [3:0] sp,
  output [3:0] sp___1_2
);

  wire or_1_out, or_2_out, sp_nop, sp_pop, sp_push, sp_reset;

  Decoder #(.select(2), .enable("false")) decoder_1 (
    .out0(sp_reset), .out1(sp_pop), .out2(sp_nop), .out3(sp_push), .sel(spsel));
  or or_1 (or_1_out, sp_push, sp_pop);
  or or_2 (or_2_out, sp_reset, sp_push);
  Counter #(.width(4), .max('hf)) u_SP (
    .load(or_2_out), .D(4'b0000), .count(or_1_out), .Q(sp), .clk(clock));  // open: carry, clr
  Adder #(.width(4)) adder_1 (.a(4'b0001), .b(sp), .out(sp___1));  // open: cin, cout
  Subtractor #(.width(4)) subtractor_1 (.a(sp), .b(4'b0001), .out(sp___1_2));  // open: bin, bout

  // Notes on the sheet:
  //   Modification de SP en fonction de SPsel
endmodule
